// Logisim project Final Project.circ as structural Verilog: 6 circuits, main circuit main
module main (
  input  [2:0] B,
  input  [2:0] A,
  input  [1:0] Select_Operation
);

  wire addition_and_subtraction_1_s0, addition_and_subtraction_1_s1, addition_and_subtraction_1_s2,
       addition_and_subtraction_1_sign, and_1_out, and_2_out, and_3_out, and_4_out, multiplexer_1_out,
       multiplexer_2_out, multiplexer_3_out, multiplexer_4_out, multiplication_1_c, multiplication_1_m0,
       multiplication_1_m1, multiplication_1_m2, multiplication_1_m3, n7448_1_p8, n7448_1_p9, n7448_1_p10,
       n7448_1_p11, n7448_1_p12, n7448_1_p13, n7448_1_p14, not_1_out, not_2_out, or_1_out, or_2_out,
       or_3_out, reminder_1_c0, reminder_1_c1, reminder_1_div0, reminder_1_sc;

  Addition_and_Subtraction addition_and_subtraction_1 (
    .A0(A[0]), .A1(A[1]), .A2(A[2]), .B0(B[0]), .B1(B[1]), .B2(B[2]),
    .Mode_of_operation(Select_Operation[0]), .S1(addition_and_subtraction_1_s1),
    .S2(addition_and_subtraction_1_s2), .S0(addition_and_subtraction_1_s0),
    .Sign(addition_and_subtraction_1_sign));
  Multiplication multiplication_1 (
    .A0(A[0]), .A1(A[1]), .A2(A[2]), .B0(B[0]), .B1(B[1]), .B2(B[2]), .M0(multiplication_1_m0),
    .M1(multiplication_1_m1), .M2(multiplication_1_m2), .M3(multiplication_1_m3), .C(multiplication_1_c));
  Reminder reminder_1 (
    .SA(A[2]), .A0(A[0]), .A1(A[1]), .SB(B[2]), .B0(B[0]), .B1(B[1]), .SC(reminder_1_sc), .C1(reminder_1_c1),
    .C0(reminder_1_c0), .Div0(reminder_1_div0));
  Multiplexer #(.select(2), .enable("false")) multiplexer_1 (
    .in0(addition_and_subtraction_1_s0), .in1(addition_and_subtraction_1_s0), .in2(multiplication_1_m0),
    .in3(reminder_1_c0), .out(multiplexer_1_out), .sel(Select_Operation));
  Multiplexer #(.select(2), .enable("false")) multiplexer_2 (
    .in0(addition_and_subtraction_1_s1), .in1(addition_and_subtraction_1_s1), .in2(multiplication_1_m1),
    .in3(reminder_1_c1), .out(multiplexer_2_out), .sel(Select_Operation));
  Multiplexer #(.select(2), .enable("false")) multiplexer_3 (
    .in0(addition_and_subtraction_1_s2), .in1(addition_and_subtraction_1_s2), .in2(multiplication_1_m2),
    .in3(1'b0), .out(multiplexer_3_out), .sel(Select_Operation));
  Multiplexer #(.select(2), .enable("false")) multiplexer_4 (
    .in0(addition_and_subtraction_1_sign), .in1(addition_and_subtraction_1_sign), .in2(multiplication_1_c),
    .in3(reminder_1_sc), .out(multiplexer_4_out), .sel(Select_Operation));
  not not_1 (not_1_out, Select_Operation[0]);
  and and_1 (and_1_out, Select_Operation[0], Select_Operation[1]);
  and and_2 (and_2_out, not_1_out, Select_Operation[1]);
  and and_3 (and_3_out, reminder_1_div0, and_1_out);
  and and_4 (and_4_out, and_2_out, multiplication_1_m3);
  LED Div_by_0 (.in(and_3_out));
  LED Negative_Sign (.in(multiplexer_4_out));
  // _7448 7448_1: pin names not known; wires that end beside it: multiplexer_2_out, multiplexer_3_out, 1'b1, and_4_out, multiplexer_1_out, 1'b0, 1'b1, n7448_1_p8, n7448_1_p9, n7448_1_p10, n7448_1_p11, n7448_1_p12, n7448_1_p13, n7448_1_p14
  _7_Segment_Display u_7_segment_display_1 (.g(multiplexer_4_out));  // open: f, a, b, e, d, c, dp
  _7_Segment_Display u_7_segment_display_2 (
    .g(n7448_1_p9), .f(n7448_1_p8), .a(n7448_1_p10), .b(n7448_1_p11), .e(n7448_1_p14), .d(n7448_1_p13),
    .c(n7448_1_p12));  // open: dp
  or or_1 (or_1_out, multiplexer_2_out, multiplexer_1_out);
  or or_2 (or_2_out, and_4_out, or_1_out);
  or or_3 (or_3_out, multiplexer_3_out, or_2_out);
  not not_2 (not_2_out, or_3_out);
  LED Zero_Flag (.in(not_2_out));
endmodule

// HA
module Half_Adder (
  input  in_1,
  input  in_2,
  output Sum,
  output Carry
);

  xor xor_1 (Sum, in_1, in_2);
  and and_1 (Carry, in_1, in_2);
endmodule

// FA
module Full_Adder (
  input  in_1,
  input  in_2,
  input  in_3,
  output Sum,
  output Carry
);

  wire half_adder_1_carry, half_adder_1_sum, half_adder_2_carry;

  Half_Adder half_adder_1 (.in_1(in_2), .in_2(in_3), .Sum(half_adder_1_sum), .Carry(half_adder_1_carry));
  Half_Adder half_adder_2 (.in_1(in_1), .in_2(half_adder_1_sum), .Sum(Sum), .Carry(half_adder_2_carry));
  or or_1 (Carry, half_adder_2_carry, half_adder_1_carry);
endmodule

// Add and Sub
module Addition_and_Subtraction (
  input  A0,
  input  A1,
  input  A2,
  input  B0,
  input  B1,
  input  B2,
  input  Mode_of_operation,
  output S1,
  output S2,
  output S0,
  output Sign
);

  wire and_1_out, and_2_out, and_3_out, and_4_out, and_5_out, and_6_out, and_7_out, and_8_out,
       full_adder_1_carry, full_adder_1_sum, full_adder_2_carry, full_adder_2_sum, half_adder_1_carry,
       not_1_out, or_1_out, or_2_out, or_4_out, xor_1_out, xor_2_out, xor_3_out, xor_4_out;

  xor xor_1 (xor_1_out, B2, Mode_of_operation);
  or or_1 (or_1_out, A1, A0);
  and and_1 (and_1_out, B0, xor_1_out);
  or or_2 (or_2_out, B1, B0);
  and and_2 (and_2_out, A0, A2);
  and and_3 (and_3_out, or_1_out, A2);
  xor xor_2 (xor_2_out, and_1_out, B1);
  and and_4 (and_4_out, or_2_out, xor_1_out);
  xor xor_3 (xor_3_out, and_2_out, A1);
  Half_Adder half_adder_1 (.in_1(A0), .in_2(B0), .Sum(S0), .Carry(half_adder_1_carry));
  Full_Adder full_adder_1 (
    .in_1(xor_3_out), .in_2(half_adder_1_carry), .in_3(xor_2_out), .Carry(full_adder_1_carry),
    .Sum(full_adder_1_sum));
  Full_Adder full_adder_2 (
    .in_1(and_3_out), .in_2(full_adder_1_carry), .in_3(and_4_out), .Carry(full_adder_2_carry),
    .Sum(full_adder_2_sum));
  not not_1 (not_1_out, xor_4_out);
  xor xor_4 (xor_4_out, and_3_out, and_4_out);
  and and_5 (and_5_out, full_adder_2_sum, xor_4_out);
  and and_6 (and_6_out, full_adder_2_carry, not_1_out);
  or or_3 (Sign, and_5_out, and_6_out);
  and and_7 (and_7_out, Sign, S0);
  and and_8 (and_8_out, full_adder_1_sum, Sign);
  xor xor_5 (S1, full_adder_1_sum, and_7_out);
  or or_4 (or_4_out, and_7_out, and_8_out);
  xor xor_6 (S2, or_4_out, full_adder_2_sum);
endmodule

// Multi
module Multiplication (
  input  A0,
  input  A1,
  input  A2,
  input  B0,
  input  B1,
  input  B2,
  output M0,
  output M1,
  output M2,
  output M3,
  output C
);

  wire and_2_out, and_3_out, and_4_out, half_adder_1_carry, or_1_out, xor_1_out;

  xor xor_1 (xor_1_out, A2, B2);
  and and_1 (M0, A0, B0);
  and and_2 (and_2_out, A1, B0);
  and and_3 (and_3_out, A0, B1);
  and and_4 (and_4_out, A1, B1);
  Half_Adder half_adder_1 (.in_1(and_2_out), .in_2(and_3_out), .Sum(M1), .Carry(half_adder_1_carry));
  Half_Adder half_adder_2 (.in_1(half_adder_1_carry), .in_2(and_4_out), .Sum(M2), .Carry(M3));
  or or_1 (or_1_out, M0, M1, M2, M3);
  and and_5 (C, xor_1_out, or_1_out);
endmodule

module Reminder (
  input  SA,
  input  A0,
  input  A1,
  input  SB,
  input  B0,
  input  B1,
  output SC,
  output C1,
  output C0,
  output Div0
);

  wire and_2_out, and_3_out, or_2_out, or_3_out;

  and and_1 (C1, B1, ~A0, A1, B0);  // AND_Gate
  and and_2 (and_2_out, ~A1, A0, B1);  // AND_Gate
  and and_3 (and_3_out, A0, B1, ~B0);  // AND_Gate
  or or_1 (C0, and_2_out, and_3_out);
  or or_2 (or_2_out, B0, B1);
  not not_1 (Div0, or_2_out);
  and and_4 (SC, SA, or_3_out);
  or or_3 (or_3_out, C1, C0);
endmodule
